# Fritzing sketch schema (saved by Fritzing 0.9.4)
breadboards: 2

parts:
  Raspberry_Pi_1 = Raspberry Pi 3 [part_number=RPI-3-V1.2]
  U = PCF8574 [package="DIP16 [THT]"]
  LCD1 = LCD screen
  V1 = DC Power [voltage=3.3V]
  V2 = DC Power [voltage=5V]
  ADC1 = MCP3008 [package=dil16]
  Q1 = NPN-Transistor [package="SOT-23 [SMD]"]
  R2 = PHOTOCELL [package=photocell]
  P1 = POT [package=pot_alpha_rv16af-20]
  R3 = Resistor [tolerance=±5% resistance=220 package="0402 [SMD]"]
  Part1 = RFID-RC522-v3
  HC-SR04_Sensor_1 = HC-SR04 Ultrasonic Distance Sensor
  R4 = Resistor [tolerance=±5% resistance=1k package=THT]
  R5 = Resistor [tolerance=±5% resistance=1k package=THT]
  BUZZ1 = Buzzer 12mm [package=buzzer-ccv]
  BREADBORD_ONLY = Breadboard Power Supply Board SMD  # not connected
  BAT1 = BC9VPC [package=bc9vpc]
  LED1 = LEDs [package=led10mm]
  LED2 = LEDs [package=led10mm]
  LED3 = LEDs [package=led10mm]
  M1 = DC Motor
  R6 = Resistor [tolerance=±5% resistance=220 package="0603 [SMD]"]
  R8 = Resistor [tolerance=±5% resistance=220 package="0603 [SMD]"]
  R7 = Resistor [tolerance=±5% resistance=220 package="0603 [SMD]"]

nets (from the schematic view):
  N1: Raspberry_Pi_1.GPIO4, Q1.0
  N2: Raspberry_Pi_1.GPIO17, LCD1.RS
  N3: Raspberry_Pi_1.GPIO27, LCD1.E
  N4: Raspberry_Pi_1.GPIO22, U.SCL
  N5: Raspberry_Pi_1.GPIO10, ADC1.Din, Part1.MOSI
  N6: Raspberry_Pi_1.GPIO9, ADC1.Dout, Part1.MISO
  N7: Raspberry_Pi_1.GPIO11, ADC1.CLK, Part1.SCK
  GND: Raspberry_Pi_1.GND, U.A0, U.A1, U.A2, U.GND, U.INT, LCD1.VSS, LCD1.LED-, V1.V-, V2.V-, ADC1.DGND, ADC1.AGND, Q1.2, R3.Pin_0, Part1.GND, HC-SR04_Sensor_1.ECHO, R5.Pin_0, BUZZ1.2, M1.pin_2, R6.Pin_1, R8.Pin_1, R7.Pin_1
  N8: Raspberry_Pi_1.GPIO5, U.SDA
  N9: Raspberry_Pi_1.GPIO20, Part1.RST
  N10: Raspberry_Pi_1.GPIO16, R4.Pin_1, R5.Pin_1
  N11: Raspberry_Pi_1.GPIO12, HC-SR04_Sensor_1.TRIG
  N12: Raspberry_Pi_1.GPIO7, Part1.SDA
  N13: Raspberry_Pi_1.GPIO8, ADC1.CS/SHDN
  N14: Raspberry_Pi_1.GPIO25, BUZZ1.1
  N15: Raspberry_Pi_1.GPIO18, LED3.A
  N16: Raspberry_Pi_1.GPIO15, LED2.A
  N17: Raspberry_Pi_1.GPIO14, LED1.A
  N18: U.P0, LCD1.DB0
  N19: U.P1, LCD1.DB1
  N20: U.P2, LCD1.DB2
  N21: U.P3, LCD1.DB3
  N22: U.P4, LCD1.DB4
  N23: U.P5, LCD1.DB5
  N24: U.P6, LCD1.DB6
  N25: U.P7, LCD1.DB7
  N26: U.VCC, V1.V+
  VDD: LCD1.VDD, LCD1.LED+, V2.V+, P1.E, HC-SR04_Sensor_1.VCC
  N27: LCD1.V0, P1.S
  N28: LCD1.R/W, P1.A
  N29: ADC1.CH0, R2.P$2, R3.Pin_1
  VDD_2: ADC1.VREF, ADC1.VDD, R2.P$1, Part1.3.3V
  N30: Q1.1, BAT1.V-
  N31: HC-SR04_Sensor_1.GND, R4.Pin_0
  N32: BAT1.V+, M1.pin_1
  N33: LED1.C, R6.Pin_0
  N34: LED2.C, R7.Pin_0
  N35: LED3.C, R8.Pin_0

custom parts:
  RFID-RC522-v3: A simple China made RFID-RC522 Reader (6x4 cm); do check the pin labels, as this is a MFRC522 based clone.
